# Fritzing sketch Circuito completo (saved by Fritzing 0.9.3b)
breadboards: 2

parts:
  Componente1 = Arduino Uno (Rev3)
  Led_Encendido = LED - 5mm [color="Green (570nm)" package="5 mm [THT]"]
  Led_Calor = LED - 5mm [color="Red (633nm)" package="5 mm [THT]"]
  Led_Frio = LED - 5mm [color="Blue (430nm)" package="5 mm [THT]"]
  R2 = Resistor [tolerance=±5% resistance=4.7k package=THT]
  R3 = Resistor [tolerance=±5% resistance=4.7k package=THT]
  R4 = Resistor [tolerance=±5% resistance=4.7k package=THT]
  R5 = Resistor [tolerance=±5% resistance=4.7k package=THT]
  Buzzer = Piezo Speaker
  Sensor_de_inclinación = Tilt Switch [package=THT]
  TMP36_Temperatura_Interna = TMP36 Temperature Sensor [package="TO92 [THT]"]
  LM35_Temperatura_Externa = LM35 Temperature Sensor [package="TO92 [THT]"]
  HC_05_Bluetooth = Bluetooth HC-05 Macho
  Peltier_TEC1-12706_Frio = Peltier Element
  Peltier_TEC1-12706_Calor = Peltier Element
  Ventilador_delantero = Basic Servo
  Fuente_12V = Power plug
  Ventilador_Trasero_2 = DC Motor
  Ventilador_Trasero_1 = DC Motor
  Q1 = Basic FET N-Channel [package="TO220 [THT]"]
  Q2 = Basic FET N-Channel [package="TO220 [THT]"]
  Q4 = PNP-Transistor [package="TO92 [THT]"]
  Q5 = TRANSISTOR_NPN [package=to-92-ammo]
  Q6 = TRANSISTOR_NPN [package=to-92-ammo]
  Q7 = PNP-Transistor [package="TO92 [THT]"]
  U1 = TRANSISTOR_NPN_2 [package=to-92]
  R6 = Resistor [tolerance=±5% resistance=4.7k package=THT]
  R7 = Resistor [tolerance=±5% resistance=4.7k package=THT]
  R8 = Resistor [tolerance=±5% resistance=4.7k package=THT]
  R9 = Resistor [tolerance=±5% resistance=4.7k package=THT]
  R10 = Resistor [tolerance=±5% resistance=4.7k package=THT]
  R11 = Resistor [tolerance=±5% resistance=4.7k package=THT]

nets:
  N1: Componente1.A0, LM35_Temperatura_Externa.Vout
  N2: Componente1.A1, TMP36_Temperatura_Interna.Vout
  N3: Componente1.A2, Ventilador_delantero.pulse
  N4: Componente1.D8, HC_05_Bluetooth.VCC
  N5: Componente1.D9_PWM, HC_05_Bluetooth.Key
  N6: Componente1.D10_PWM/SS, HC_05_Bluetooth.TXD
  N7: Componente1.D11_PWM/MOSI, HC_05_Bluetooth.RXD
  N8: Componente1.D12/MISO, R3.Pin_1
  N9: Componente1.D13/SCK, R2.Pin_1
  GND: Componente1.GND, Led_Encendido.cathode, Led_Calor.cathode, Led_Frio.cathode, Buzzer.pin1, Sensor_de_inclinación.Pin_1, TMP36_Temperatura_Interna.GND, LM35_Temperatura_Externa.GND
  N10: Componente1.D2, R5.Pin_1
  N11: Componente1.D3_PWM, Buzzer.pin2
  N12: Componente1.D4, R4.Pin_1
  N13: Componente1.D5_PWM, U1.B
  N14: Componente1.D6_PWM, R11.Pin_1
  N15: Componente1.D7, R8.Pin_1
  N16: Componente1.5V, TMP36_Temperatura_Interna.+Vs, LM35_Temperatura_Externa.+Vs
  N17: Led_Encendido.anode, R4.Pin_0
  N18: Led_Calor.anode, R2.Pin_0
  N19: Led_Frio.anode, R3.Pin_0
  N20: R5.Pin_0, Sensor_de_inclinación.Pin_2
  GND_2: HC_05_Bluetooth.GND, Peltier_TEC1-12706_Frio.pin1, Peltier_TEC1-12706_Calor.pin1, Ventilador_delantero.gnd, Fuente_12V.GND, Ventilador_Trasero_1.pin_1, Q1.drain, Q2.drain, Q5.E, Q6.E, R6.Pin_1, R9.Pin_1
  N21: Peltier_TEC1-12706_Frio.pin2, Q1.source
  N22: Peltier_TEC1-12706_Calor.pin2, Q2.source
  N23: Ventilador_delantero.vcc, U1.C
  N24: Fuente_12V.VCC, Ventilador_Trasero_2.pin_1, Ventilador_Trasero_2.pin_2, Ventilador_Trasero_1.pin_2, Q4.B, Q7.B, U1.E
  N25: Q1.gate, Q7.E, R6.Pin_0
  N26: Q2.gate, Q4.E, R9.Pin_0
  N27: Q4.C, R10.Pin_0
  N28: Q5.B, R11.Pin_0
  N29: Q5.C, R10.Pin_1
  N30: Q6.B, R8.Pin_0
  N31: Q6.C, R7.Pin_1
  N32: Q7.C, R7.Pin_0
